# Fritzing sketch encoder (saved by Fritzing 0.9.3b)
breadboards: 1

parts:
  RE1 = Rotary Encoder [package=THT]
  Pro_Micro1 = Pro Micro

nets:
  N1: RE1.EncoderPinA, Pro_Micro1.D4
  N2: RE1.EncoderPinC, Pro_Micro1.GND
  N3: RE1.EncoderPinB, Pro_Micro1.D2

custom parts:
  Pro Micro: The SparkFun Pro Micro is a complete USB-based microcontoller development system, in a very small footprint, capable of implementing many types of projects. All programming can be done via the USB port.
